# Fritzing sketch PISO using cd4014bm (saved by Fritzing 0.9.2b)
breadboards: 1

parts:
  IC1 = IC, DIP package, 16 pins [chip_label="IC CD4014BM"]
  Part1 = Arduino Uno (Rev3)
  LED1 = LED - 5mm [color="Red (633nm)" package="5 mm [THT]"]
  R1 = Resistor [tolerance=±5% resistance=10k package=THT]
  R2 = Resistor [tolerance=±5% resistance=10k package=THT]
  S1 = Pushbutton [package="[THT]"]
  S2 = Pushbutton [package="[THT]"]
  S3 = Pushbutton [package="[THT]"]
  S4 = Pushbutton [package="[THT]"]
  S5 = Pushbutton [package="[THT]"]
  S6 = Pushbutton [package="[THT]"]
  S7 = Pushbutton [package="[THT]"]
  S8 = Pushbutton [package="[THT]"]
  R = Resistor [tolerance=±5% resistance=10k package=THT]
  R4 = Resistor [tolerance=±5% resistance=10k package=THT]
  R5 = Resistor [tolerance=±5% resistance=10k package=THT]
  R6 = Resistor [tolerance=±5% resistance=10k package=THT]
  R7 = Resistor [tolerance=±5% resistance=10k package=THT]
  R8 = Resistor [tolerance=±5% resistance=10k package=THT]
  R9 = Resistor [tolerance=±5% resistance=10k package=THT]
  R10 = Resistor [tolerance=±5% resistance=10k package=THT]
  LED2 = LED - 5mm [color="Red (633nm)" package="5 mm [THT]"]

nets:
  N1: IC1.pin1, S7.Pin_3, S7.Pin_4, R.Pin_1
  N2: IC1.pin3, Part1.D9_PWM
  N3: IC1.pin4, S3.Pin_3, S3.Pin_4, R7.Pin_1
  N4: IC1.pin5, S2.Pin_3, S2.Pin_4, R8.Pin_1
  N5: IC1.pin6, S1.Pin_3, S1.Pin_4, R9.Pin_1
  N6: IC1.pin7, S8.Pin_3, S8.Pin_4, R10.Pin_1
  N7: IC1.pin8, IC1.pin11, Part1.GND, LED1.cathode, R.Pin_0, R4.Pin_0, R5.Pin_0, R6.Pin_0, R7.Pin_0, R8.Pin_0, R9.Pin_0, R10.Pin_0, LED2.cathode
  N8: IC1.pin9, Part1.D11_PWM/MOSI
  N9: IC1.pin10, Part1.D10_PWM/SS
  N10: IC1.pin13, S4.Pin_3, S4.Pin_4, R6.Pin_1
  N11: IC1.pin14, S5.Pin_3, S5.Pin_4, R5.Pin_1
  N12: IC1.pin15, S6.Pin_3, S6.Pin_4, R4.Pin_1
  N13: IC1.pin16, Part1.5V, S1.Pin_1, S1.Pin_2, S2.Pin_1, S2.Pin_2, S3.Pin_1, S3.Pin_2, S4.Pin_1, S4.Pin_2, S5.Pin_1, S5.Pin_2, S6.Pin_1, S6.Pin_2, S7.Pin_1, S7.Pin_2, S8.Pin_1, S8.Pin_2
  N14: Part1.D5_PWM, R2.Pin_0
  N15: Part1.D6_PWM, R1.Pin_0
  N16: LED1.anode, R1.Pin_1
  N17: R2.Pin_1, LED2.anode

notes:
  Clock LED
  Output LED
  MSB input
  LSB input
