# Fritzing sketch SIPO_using_74HC595 (saved by Fritzing 0.9.2b)
breadboards: 1

parts:
  LED1 = LED - 5mm [color="Red (633nm)" package="5 mm [THT]"]
  LED2 = LED - 5mm [color="Red (633nm)" package="5 mm [THT]"]
  LED3 = LED - 5mm [color="Red (633nm)" package="5 mm [THT]"]
  LED4 = LED - 5mm [color="Red (633nm)" package="5 mm [THT]"]
  LED5 = LED - 5mm [color="Red (633nm)" package="5 mm [THT]"]
  LED6 = LED - 5mm [color="Red (633nm)" package="5 mm [THT]"]
  LED7 = LED - 5mm [color="Red (633nm)" package="5 mm [THT]"]
  LED8 = LED - 5mm [color="Red (633nm)" package="5 mm [THT]"]
  R = Resistor [tolerance=±5% resistance=10k package=THT]
  R2 = Resistor [tolerance=±5% resistance=10k package=THT]
  R3 = Resistor [tolerance=±5% resistance=10k package=THT]
  R4 = Resistor [tolerance=±5% resistance=10k package=THT]
  R5 = Resistor [tolerance=±5% resistance=10k package=THT]
  R6 = Resistor [tolerance=±5% resistance=10k package=THT]
  R7 = Resistor [tolerance=±5% resistance=10k package=THT]
  R8 = Resistor [tolerance=±5% resistance=10k package=THT]
  S1 = Pushbutton [package="[THT]"]
  R9 = Resistor [tolerance=±5% resistance=10k package=THT]
  U1 = 74HC595 [package="DIP16 [THT]"]
  Part1 = Arduino Uno (Rev3)

nets:
  GND: LED1.cathode, LED2.cathode, LED3.cathode, LED4.cathode, LED5.cathode, LED6.cathode, LED7.cathode, LED8.cathode, R9.Pin_0, U1.GND, U1.OE, Part1.GND
  N1: LED1.anode, R.Pin_1
  N2: LED2.anode, R2.Pin_1
  N3: LED3.anode, R3.Pin_1
  N4: LED4.anode, R4.Pin_1
  N5: LED5.anode, R5.Pin_1
  N6: LED6.anode, R6.Pin_1
  N7: LED7.anode, R7.Pin_1
  N8: LED8.anode, R8.Pin_1
  N9: R.Pin_0, U1.Q7
  N10: R2.Pin_0, U1.Q6
  N11: R3.Pin_0, U1.Q5
  N12: R4.Pin_0, U1.Q4
  N13: R5.Pin_0, U1.Q3
  N14: R6.Pin_0, U1.Q2
  N15: R7.Pin_0, U1.Q1
  N16: R8.Pin_0, U1.Q0
  VCC: S1.Pin_1, S1.Pin_2, U1.MR, U1.VCC, Part1.5V
  N17: S1.Pin_3, S1.Pin_4, R9.Pin_1, Part1.D5_PWM
  N18: U1.SH_CP, Part1.D9_PWM
  N19: U1.ST_CP, Part1.D10_PWM/SS
  N20: U1.DS, Part1.D11_PWM/MOSI

notes:
  LSB
  MSB
  external Serial input
