# Fritzing sketch SISO (saved by Fritzing 0.9.2b)
breadboards: 1

parts:
  Part1 = Arduino Uno (Rev3)
  LED1 = LED - 5mm [color="Red (633nm)" package="5 mm [THT]"]
  R1 = Resistor [tolerance=±5% resistance=10k package=THT]
  S1 = Pushbutton [package="[THT]"]
  R = Resistor [tolerance=±5% resistance=10k package=THT]
  S2 = Pushbutton [package="[THT]"]
  R3 = Resistor [tolerance=±5% resistance=10k package=THT]

nets:
  N1: Part1.D9_PWM, R1.Pin_0
  N2: Part1.D2, S2.Pin_3, S2.Pin_4, R3.Pin_1
  N3: Part1.D5_PWM, S1.Pin_3, S1.Pin_4, R.Pin_1
  N4: Part1.5V, S1.Pin_1, S1.Pin_2, S2.Pin_1, S2.Pin_2
  N5: Part1.GND, LED1.cathode, R.Pin_0, R3.Pin_0
  N6: LED1.anode, R1.Pin_1

notes:
  Serial out
  Serial in
  External clock
