# Fritzing sketch DEMUX 1-4 (saved by Fritzing 0.9.2b)
breadboards: 1

parts:
  Part1 = Arduino Uno (Rev3)
  S1 = Pushbutton [package="[THT]"]
  S2 = Pushbutton [package="[THT]"]
  S3 = Pushbutton [package="[THT]"]
  R = Resistor [tolerance=±5% resistance=10k package=THT]
  R2 = Resistor [tolerance=±5% resistance=10k package=THT]
  R3 = Resistor [tolerance=±5% resistance=10k package=THT]
  LED1 = LED - 5mm [color="Red (633nm)" package="5 mm [THT]"]
  LED2 = LED - 5mm [color="Red (633nm)" package="5 mm [THT]"]
  LED3 = LED - 5mm [color="Red (633nm)" package="5 mm [THT]"]
  LED4 = LED - 5mm [color="Red (633nm)" package="5 mm [THT]"]
  R4 = Resistor [tolerance=±5% resistance=10k package=THT]
  R5 = Resistor [tolerance=±5% resistance=10k package=THT]
  R6 = Resistor [tolerance=±5% resistance=10k package=THT]
  R7 = Resistor [tolerance=±5% resistance=10k package=THT]

nets:
  N1: Part1.D9_PWM, R5.Pin_0
  N2: Part1.D10_PWM/SS, R6.Pin_0
  N3: Part1.D11_PWM/MOSI, R7.Pin_0
  N4: Part1.GND, R.Pin_0, R2.Pin_0, R3.Pin_0, LED1.cathode, LED2.cathode, LED3.cathode, LED4.cathode
  N5: Part1.D5_PWM, S3.Pin_3, S3.Pin_4, R3.Pin_1
  N6: Part1.D6_PWM, S1.Pin_3, S1.Pin_4, R2.Pin_1
  N7: Part1.D7, S2.Pin_3, S2.Pin_4, R.Pin_1
  N8: Part1.5V, S1.Pin_1, S1.Pin_2, S2.Pin_1, S2.Pin_2, S3.Pin_1, S3.Pin_2
  N9: LED1.anode, R4.Pin_1
  N10: LED2.anode, R7.Pin_1
  N11: LED3.anode, R6.Pin_1
  N12: LED4.anode, R5.Pin_1

notes:
  B Select Lines A
  Input
  L3                Outputs                L0
