# Fritzing sketch Decimal to binary encoder (0 to 7) (saved by Fritzing 0.9.2b)
breadboards: 1

parts:
  Part1 = Arduino Uno (Rev3)
  S1 = Pushbutton [package="[THT]"]
  S2 = Pushbutton [package="[THT]"]
  S3 = Pushbutton [package="[THT]"]
  S4 = Pushbutton [package="[THT]"]
  S5 = Pushbutton [package="[THT]"]
  S6 = Pushbutton [package="[THT]"]
  S7 = Pushbutton [package="[THT]"]
  LED1 = LED - 5mm [color="Red (633nm)" package="5 mm [THT]"]
  LED2 = LED - 5mm [color="Red (633nm)" package="5 mm [THT]"]
  LED3 = LED - 5mm [color="Red (633nm)" package="5 mm [THT]"]
  R1 = Resistor [tolerance=±5% resistance=10k package=THT]
  R2 = Resistor [tolerance=±5% resistance=10k package=THT]
  R3 = Resistor [tolerance=±5% resistance=10k package=THT]
  R = Resistor [tolerance=±5% resistance=10k package=THT]
  R5 = Resistor [tolerance=±5% resistance=10k package=THT]
  R6 = Resistor [tolerance=±5% resistance=10k package=THT]
  R7 = Resistor [tolerance=±5% resistance=10k package=THT]
  R8 = Resistor [tolerance=±5% resistance=10k package=THT]
  R9 = Resistor [tolerance=±5% resistance=10k package=THT]
  R10 = Resistor [tolerance=±5% resistance=10k package=THT]

nets:
  N1: Part1.D8, S7.Pin_3, S7.Pin_4, R.Pin_1
  N2: Part1.D10_PWM/SS, R3.Pin_0
  N3: Part1.D11_PWM/MOSI, R2.Pin_0
  N4: Part1.D12/MISO, R1.Pin_0
  N5: Part1.D2, S1.Pin_3, S1.Pin_4, R10.Pin_1
  N6: Part1.D3_PWM, S2.Pin_3, S2.Pin_4, R9.Pin_1
  N7: Part1.D4, S3.Pin_3, S3.Pin_4, R8.Pin_1
  N8: Part1.D5_PWM, S4.Pin_3, S4.Pin_4, R6.Pin_1
  N9: Part1.D6_PWM, S5.Pin_3, S5.Pin_4, R5.Pin_1
  N10: Part1.D7, S6.Pin_3, S6.Pin_4, R7.Pin_1
  N11: Part1.5V, S1.Pin_1, S1.Pin_2, S2.Pin_1, S2.Pin_2, S3.Pin_1, S3.Pin_2, S4.Pin_1, S4.Pin_2, S5.Pin_1, S5.Pin_2, S6.Pin_1, S6.Pin_2, S7.Pin_1, S7.Pin_2
  N12: Part1.GND, LED1.cathode, LED2.cathode, LED3.cathode, R.Pin_0, R5.Pin_0, R8.Pin_0, R10.Pin_0
  N13: LED1.anode, R1.Pin_1
  N14: LED2.anode, R3.Pin_1
  N15: LED3.anode, R2.Pin_1

notes:
  7                      INPUTS                      1
  MSB       OUTPUTS       LSB
