# Fritzing sketch D FF (saved by Fritzing 0.9.2b)
breadboards: 1

parts:
  Part1 = Arduino Uno (Rev3)
  LED1 = LED - 5mm [color="Red (633nm)" package="5 mm [THT]"]
  R1 = Resistor [tolerance=±5% resistance=10k package=THT]
  S2 = Pushbutton [package="[THT]"]
  R4 = Resistor [tolerance=±5% resistance=10k package=THT]
  LED2 = LED - 5mm [color="Red (633nm)" package="5 mm [THT]"]
  R2 = Resistor [tolerance=±5% resistance=10k package=THT]

nets:
  N1: Part1.D9_PWM, R1.Pin_0
  N2: Part1.D10_PWM/SS, R2.Pin_0
  N3: Part1.D5_PWM, S2.Pin_3, S2.Pin_4, R4.Pin_1
  N4: Part1.5V, S2.Pin_1, S2.Pin_2
  N5: Part1.GND, LED1.cathode, R4.Pin_0, LED2.cathode
  N6: LED1.anode, R1.Pin_1
  N7: LED2.anode, R2.Pin_1

notes:
  Q
  D
  !Q
