# Fritzing sketch LOGIC GATES (1 input) (saved by Fritzing 0.9.2b)
breadboards: 1

parts:
  Part1 = Arduino Uno (Rev3)
  S2 = Pushbutton [package="[THT]"]
  LED1 = LED - 5mm [color="Red (633nm)" package="5 mm [THT]"]
  R = Resistor [tolerance=±5% resistance=10k package=THT]
  R3 = Resistor [tolerance=±5% resistance=10k package=THT]

nets:
  N1: Part1.D9_PWM, R3.Pin_0
  N2: Part1.D5_PWM, S2.Pin_3, S2.Pin_4, R.Pin_1
  N3: Part1.5V, S2.Pin_1, S2.Pin_2
  N4: Part1.GND, LED1.cathode, R.Pin_0
  N5: LED1.anode, R3.Pin_1
