# Fritzing sketch MUX 4-1 (saved by Fritzing 0.9.2b)
breadboards: 1

parts:
  Part1 = Arduino Uno (Rev3)
  R1 = Resistor [tolerance=±5% resistance=10k package=THT]
  S1 = Pushbutton [package="[THT]"]
  LED1 = LED - 5mm [color="Red (633nm)" package="5 mm [THT]"]
  S2 = Pushbutton [package="[THT]"]
  S3 = Pushbutton [package="[THT]"]
  S4 = Pushbutton [package="[THT]"]
  S5 = Pushbutton [package="[THT]"]
  S6 = Pushbutton [package="[THT]"]
  R = Resistor [tolerance=±5% resistance=10k package=THT]
  R3 = Resistor [tolerance=±5% resistance=10k package=THT]
  R4 = Resistor [tolerance=±5% resistance=10k package=THT]
  R5 = Resistor [tolerance=±5% resistance=10k package=THT]
  R6 = Resistor [tolerance=±5% resistance=10k package=THT]
  R7 = Resistor [tolerance=±5% resistance=10k package=THT]

nets:
  N1: Part1.D9_PWM, R1.Pin_0
  N2: Part1.D2, S5.Pin_3, S5.Pin_4, R7.Pin_1
  N3: Part1.D3_PWM, S6.Pin_1, S6.Pin_2, R6.Pin_1
  N4: Part1.D4, S4.Pin_3, S4.Pin_4, R5.Pin_1
  N5: Part1.D5_PWM, S3.Pin_3, S3.Pin_4, R4.Pin_1
  N6: Part1.D6_PWM, S2.Pin_3, S2.Pin_4, R3.Pin_1
  N7: Part1.D7, S1.Pin_3, S1.Pin_4, R.Pin_1
  N8: Part1.5V, S1.Pin_1, S1.Pin_2, S2.Pin_1, S2.Pin_2, S3.Pin_1, S3.Pin_2, S4.Pin_1, S4.Pin_2, S5.Pin_1, S5.Pin_2, S6.Pin_3, S6.Pin_4
  N9: Part1.GND, LED1.cathode, R.Pin_0, R3.Pin_0, R4.Pin_0, R5.Pin_0, R6.Pin_0, R7.Pin_0
  N10: R1.Pin_1, LED1.anode

notes:
  I3          Inputs          I0
  B Select Lines A
  Output
